// Logisim project MahyarMohammadi-610398166.circ as structural Verilog: 31 circuits, main circuit main
module main (
  output [15:0] out_1,
  output [15:0] out_2,
  output [15:0] out_3,
  output [15:0] out_4,
  output [15:0] out_5,
  output [15:0] out_6,
  output [7:0] out_7
);

  wire ac_alu_controler_1_clear_ac, ac_alu_controler_1_increment_ac, ALU_E_OUT, and_1_out,
       ar_controler_1_clr, ar_controler_1_inr, ar_controler_1_load, CLK, clock_1_out, dr_controler_1_inr,
       dr_controler_1_load, E, e_controler_1_j, e_controler_1_k, FGI, fgi_controler_1_j, fgi_controler_1_k,
       FGO, fgo_controler_1_j, fgo_controler_1_k, HALT_q, I, i_controler_1_j, i_controler_1_k, IEN,
       ien_controler_1_j, ien_controler_1_k, ir_controler_1_load, memory_controler_1_read,
       memory_controler_1_write, not_1_out, not_2_out, not_3_out, or_1_out, or_2_out, outr_controler_1_load,
       pc_controler_1_clr, pc_controler_1_inr, pc_controler_1_load, R, r_controler_1_j, r_controler_1_k, S,
       s_controler_1_j, s_controler_1_k, sc_clear_controler_1_clear, tr_controler_1_load;
  wire [2:0] bus_controler_1_out_5;
  wire [3:0] Seq;
  wire [6:0] ac_alu_controler_1_and;
  wire [7:0] inpr_1_out_1;
  wire [15:0] alu_16bit_1_aluoutput, ram_1_data, tr_1_output;

  R_Controler r_controler_1 (
    .in_1(out_5), .IEN(IEN), .FGI(FGI), .FGO(FGO), .SeqCntrInp(Seq), .in_5(R), .J(r_controler_1_j),
    .K(r_controler_1_k));
  I_Controler i_controler_1 (
    .in_1(out_5), .SeqCntrInp(Seq), .in_2(R), .in_3(I), .J(i_controler_1_j), .K(i_controler_1_k));
  E_Controler e_controler_1 (
    .in_1(out_5), .SeqCntrInp(Seq), .J(e_controler_1_j), .in_3(R), .in_4(I), .K(e_controler_1_k),
    .in_2(ALU_E_OUT));
  S_Controler s_controler_1 (
    .in_1(out_5), .SeqCntrInp(Seq), .J(s_controler_1_j), .K(s_controler_1_k), .in_2(R), .in_3(I));
  IEN_Controler ien_controler_1 (
    .in_1(out_5), .SeqCntrInp(Seq), .J(ien_controler_1_j), .K(ien_controler_1_k), .in_2(R), .in_3(I));
  FGI_Controler fgi_controler_1 (
    .in_1(out_5), .SeqCntrInp(Seq), .J(fgi_controler_1_j), .K(fgi_controler_1_k), .in_2(R), .in_3(I));
  FGO_Controler fgo_controler_1 (
    .in_1(out_5), .SeqCntrInp(Seq), .J(fgo_controler_1_j), .K(fgo_controler_1_k), .in_2(R), .in_3(I));
  J_K_Flip_Flop u_R (.J(r_controler_1_j), .clk(CLK), .K(r_controler_1_k), .Q(R));  // open: Qn, preset, en, reset
  J_K_Flip_Flop u_I (.J(i_controler_1_j), .clk(CLK), .K(i_controler_1_k), .Q(I));  // open: Qn, preset, en, reset
  J_K_Flip_Flop u_E (.J(e_controler_1_j), .clk(CLK), .K(e_controler_1_k), .Q(E));  // open: Qn, preset, en, reset
  J_K_Flip_Flop u_S (.J(s_controler_1_j), .clk(CLK), .K(s_controler_1_k), .Qn(S));  // open: Q, preset, en, reset
  J_K_Flip_Flop u_IEN (
    .J(ien_controler_1_j), .clk(CLK), .K(ien_controler_1_k), .Q(IEN));  // open: Qn, preset, en, reset
  J_K_Flip_Flop u_FGI (
    .J(fgi_controler_1_j), .clk(CLK), .K(fgi_controler_1_k), .Q(FGI));  // open: Qn, preset, en, reset
  J_K_Flip_Flop u_FGO (
    .J(fgo_controler_1_j), .clk(CLK), .K(fgo_controler_1_k), .Q(FGO));  // open: Qn, preset, en, reset
  Clock clock_1 (.out(clock_1_out));
  SC_Clear_Controler sc_clear_controler_1 (
    .in_1(out_5), .SeqCntrInp(Seq), .in_2(R), .Clear(sc_clear_controler_1_clear), .in_3(I));
  and and_1 (and_1_out, clock_1_out, S);
  not not_1 (not_1_out, S);
  or or_1 (or_1_out, not_1_out, HALT_q);
  Counter #(.width(4), .max('hf)) sequenceCounter (
    .load(sc_clear_controler_1_clear), .D(4'b0000), .count(not_2_out), .Q(Seq), .clk(CLK));  // open: carry, clr
  not not_2 (not_2_out, sc_clear_controler_1_clear);
  not not_3 (not_3_out, HALT_q);
  J_K_Flip_Flop HALT (.J(or_1_out), .clk(clock_1_out), .K(1'b0), .Q(HALT_q));  // open: Qn, preset, en, reset
  and and_2 (CLK, and_1_out, not_3_out);
  INPR inpr_1 (.out_1(inpr_1_out_1));
  AC_ALU_Controler ac_alu_controler_1 (
    .in_1(out_5), .SeqCntrInp(Seq), .AND(ac_alu_controler_1_and[0]), .ADD(ac_alu_controler_1_and[1]),
    .DR(ac_alu_controler_1_and[2]), .INPR(ac_alu_controler_1_and[3]), .COM(ac_alu_controler_1_and[4]),
    .SHR(ac_alu_controler_1_and[5]), .SHL(ac_alu_controler_1_and[6]),
    .INCREMENT_AC(ac_alu_controler_1_increment_ac), .CLEAR_AC(ac_alu_controler_1_clear_ac), .in_2(R), .in_3(I));
  ALU_16bit alu_16bit_1 (
    .AC(out_4), .AND(ac_alu_controler_1_and[0]), .ADD(ac_alu_controler_1_and[1]),
    .DR_2(ac_alu_controler_1_and[2]), .INPR_2(ac_alu_controler_1_and[3]), .COM(ac_alu_controler_1_and[4]),
    .SHR(ac_alu_controler_1_and[5]), .SHL(ac_alu_controler_1_and[6]), .DR(out_3), .INPR(inpr_1_out_1),
    .ALUOutput(alu_16bit_1_aluoutput), .E_2(ALU_E_OUT), .E(E));
  Memory_Controler memory_controler_1 (
    .in_1(out_5), .SeqCntrInp(Seq), .in_2(R), .Write(memory_controler_1_write),
    .Read(memory_controler_1_read), .in_3(I));
  AR_Controler ar_controler_1 (
    .in_1(out_5), .SeqCntrInp(Seq), .Load(ar_controler_1_load), .INR(ar_controler_1_inr),
    .CLR(ar_controler_1_clr), .in_2(R), .in_3(I));
  PC_Controler pc_controler_1 (
    .IR(out_5), .SeqCntrInp(Seq), .Load(pc_controler_1_load), .INR(pc_controler_1_inr),
    .CLR(pc_controler_1_clr), .in_7(R), .AC(out_4), .DR(out_3), .FGI(FGI), .FGO(FGO), .E(E), .in_8(I));
  DR_Controler dr_controler_1 (
    .in_1(out_5), .in_2(R), .SeqCntrInp(Seq), .Load(dr_controler_1_load), .INR(dr_controler_1_inr), .in_3(I));
  or or_2 (or_2_out, ac_alu_controler_1_and[0], ac_alu_controler_1_and[1], ac_alu_controler_1_and[2], ac_alu_controler_1_and[3], ac_alu_controler_1_and[4], ac_alu_controler_1_and[5], ac_alu_controler_1_and[6]);
  IR_Controler ir_controler_1 (.in_1(out_5), .in_2(R), .SeqCntrInp(Seq), .Load(ir_controler_1_load), .in_3(I));
  TR_Controler tr_controler_1 (.in_1(out_5), .SeqCntrInp(Seq), .Load(tr_controler_1_load), .in_2(R), .in_3(I));
  OUTR outr_1 (.\input (out_6), .Load(outr_controler_1_load), .CLK(CLK), .out_4(out_7));
  OUTR_Controler outr_controler_1 (.in_1(out_5), .SeqCntrInp(Seq), .Load(outr_controler_1_load), .in_2(R), .in_3(I));
  RAM #(.addrWidth(12), .dataWidth(16), .bus("separate")) ram_1 (
    .addr(out_1[11:0]), .din(out_6), .data(ram_1_data), .str(memory_controler_1_write), .clk(CLK),
    .ld(memory_controler_1_read));  // open: sel, clr
  // Probe on out_1
  AR ar_1 (
    .\input (out_6), .Output(out_1), .Load(ar_controler_1_load), .INC(ar_controler_1_inr),
    .Clear(ar_controler_1_clr), .CLK(CLK));
  PC pc_1 (
    .\input (out_6), .Output(out_2), .Load(pc_controler_1_load), .INC(pc_controler_1_inr),
    .Clear(pc_controler_1_clr), .CLK(CLK));
  DR dr_1 (
    .\input (out_6), .Output(out_3), .Load(dr_controler_1_load), .INC(dr_controler_1_inr), .CLK(CLK));  // open: Clear
  AC ac_1 (
    .\input (alu_16bit_1_aluoutput), .Output(out_4), .Load(or_2_out), .INC(ac_alu_controler_1_increment_ac),
    .Clear(ac_alu_controler_1_clear_ac), .CLK(CLK));
  IR ir_1 (.\input (out_6), .Output(out_5), .Load(ir_controler_1_load), .CLK(CLK));
  TR tr_1 (.\input (out_6), .Output(tr_1_output), .Load(tr_controler_1_load), .CLK(CLK));  // open: INC, Clear
  Bus_Controler bus_controler_1 (.in_1(out_5), .SeqCntrInp(Seq), .out_5(bus_controler_1_out_5), .in_2(R), .in_3(I));
  // Probe on out_4
  BUS bus_1 (
    .input1(out_1), .input2(out_2), .input3(out_3), .input4(out_4), .input5(out_5), .input6(tr_1_output),
    .input7(ram_1_data), .out_12(out_6), .S2(bus_controler_1_out_5[2]), .S1(bus_controler_1_out_5[1]),
    .S0(bus_controler_1_out_5[0]));  // open: input0

  // Other names for the same wires on the sheet: IR[15:0] = out_5

  // Notes on the sheet:
  //   All Flip Flops
  //   |
  //   |
  //   |
  //   |
  //   |
  //   |
  //   |
  //   |
  //   _
  //   _
  //   _
  //   _
  //   _
  //   _
  //   _
  //   _
  //   _
  //   _
  //   _
  //   _
  //   _
  //   _
  //   _
  //   |
  //   |
  //   |
  //   |
  //   |
  //   |
  //   |
  //   |
  //   |
  //   |
  //   |
  //   |
  //   |
  //   |
  //   |
  //   |
  //   |
  //   |
  //   |
  //   |
  //   |
  //   |
  //   |
  //   |
  //   |
  //   _
  //   _
  //   _
  //   _
  //   _
  //   _
  //   _
  //   _
  //   _
  //   _
  //   _
  //   _
  //   _
  //   Clock Pulse
  //   Sequence Counter
  //   _
  //   _
  //   _
  //   _
  //   _
  //   _
  //   _
  //   _
  //   _
  //   _
  //   _
  //   _
  //   _
  //   _
  //   _
  //   _
  //   _
  //   _
  //   _
  //   _
  //   _
  //   _
  //   _
  //   _
  //   _
  //   _
  //   _
  //   |
  //   |
  //   |
  //   |
  //   |
  //   |
  //   |
  //   |
  //   _
  //   |
  //   |
  //   |
  //   |
  //   |
  //   |
  //   |
  //   |
  //   |
  //   |
  //   |
  //   |
  //   |
  //   |
  //   |
  //   |
  //   |
  //   |
  //   |
  //   |
  //   |
  //   |
  //   |
  //   |
  //   |
endmodule

module BUS (
  input  [15:0] input0,
  input  [15:0] input1,
  input  [15:0] input2,
  input  [15:0] input3,
  input  [15:0] input4,
  input  [15:0] input5,
  input  [15:0] input6,
  input  [15:0] input7,
  input  S2,
  input  S1,
  input  S0,
  output [15:0] out_12
);

  Multiplexer #(.select(3), .width(16), .enable("false")) multiplexer_1 (
    .in0(input0), .in1(input1), .in2(input2), .in3(input3), .in4(input4), .in5(input5), .in6(input6),
    .in7(input7), .out(out_12), .sel({S2, S1, S0}));
endmodule

module FA (
  input  x,
  input  carryIN,
  input  y,
  output S,
  output carryOut
);

  wire decoder_1_out1, decoder_1_out2, decoder_1_out3, decoder_1_out4, decoder_1_out5, decoder_1_out6,
       decoder_1_out7;

  Decoder #(.select(3), .enable("false")) decoder_1 (
    .out1(decoder_1_out1), .out2(decoder_1_out2), .out3(decoder_1_out3), .out4(decoder_1_out4),
    .out5(decoder_1_out5), .out6(decoder_1_out6), .out7(decoder_1_out7), .sel({x, y, carryIN}));  // open: out0
  or or_1 (S, decoder_1_out1, decoder_1_out2, decoder_1_out4, decoder_1_out7);
  or or_2 (carryOut, decoder_1_out3, decoder_1_out5, decoder_1_out6, decoder_1_out7);
endmodule

module ALU_1bit (
  input  DR_i,
  input  AC_i,
  input  AND,
  input  ADD,
  input  DR,
  input  c_i,
  input  INPR,
  input  INPR_in,
  input  COM,
  input  SHR,
  input  AC_i_1,
  input  SHL,
  input  AC_i_1_2,
  output c_i_1,
  output OUT
);

  wire and_1_out, and_2_out, and_3_out, and_4_out, and_5_out, and_6_out, and_7_out, fa_1_s, not_1_out;

  FA fa_1 (.x(AC_i), .S(fa_1_s), .carryOut(c_i_1), .carryIN(c_i), .y(DR_i));
  not not_1 (not_1_out, AC_i);
  and and_1 (and_1_out, AND, AC_i, DR_i);
  and and_2 (and_2_out, ADD, fa_1_s);
  and and_3 (and_3_out, DR, DR_i);
  and and_4 (and_4_out, INPR, INPR_in);
  and and_5 (and_5_out, COM, not_1_out);
  and and_6 (and_6_out, SHR, AC_i_1);
  and and_7 (and_7_out, SHL, AC_i_1_2);
  or or_1 (OUT, and_1_out, and_2_out, and_3_out, and_4_out, and_5_out, and_6_out, and_7_out);
endmodule

module ALU_16bit (
  input  [15:0] AC,
  input  [15:0] DR,
  input  [7:0] INPR,
  input  AND,
  input  ADD,
  input  DR_2,
  input  INPR_2,
  input  COM,
  input  SHR,
  input  SHL,
  input  E,
  output [15:0] ALUOutput,
  output E_2
);

  wire _3_c_i_1, alu_1bit_1_c_i_1, alu_1bit_2_c_i_1, alu_1bit_3_c_i_1, alu_1bit_4_c_i_1, alu_1bit_5_c_i_1,
       alu_1bit_6_c_i_1, alu_1bit_7_c_i_1, alu_1bit_8_c_i_1, alu_1bit_9_c_i_1, alu_1bit_10_c_i_1,
       alu_1bit_11_c_i_1, alu_1bit_12_c_i_1, alu_1bit_13_c_i_1, alu_1bit_14_c_i_1, alu_1bit_15_c_i_1,
       and_1_out, and_2_out, and_3_out, and_4_out, isShift, not_1_out, Shift;

  or or_1 (isShift, SHR, SHL);
  and and_1 (and_1_out, SHL, AC[15]);
  and and_2 (and_2_out, SHR, AC[0]);
  or or_2 (Shift, and_1_out, and_2_out);
  ALU_1bit alu_1bit_1 (
    .AND(AND), .ADD(ADD), .DR(DR_2), .c_i(1'b0), .INPR(INPR_2), .INPR_in(INPR[0]), .COM(COM), .SHR(SHR),
    .AC_i_1(AC[1]), .SHL(SHL), .AC_i_1_2(E), .c_i_1(alu_1bit_1_c_i_1), .OUT(ALUOutput[0]), .DR_i(DR[0]),
    .AC_i(AC[0]));
  ALU_1bit alu_1bit_2 (
    .AND(AND), .ADD(ADD), .DR(DR_2), .c_i(alu_1bit_1_c_i_1), .INPR(INPR_2), .INPR_in(INPR[1]), .COM(COM),
    .SHR(SHR), .AC_i_1(AC[2]), .SHL(SHL), .AC_i_1_2(AC[0]), .c_i_1(alu_1bit_2_c_i_1), .OUT(ALUOutput[1]),
    .DR_i(DR[1]), .AC_i(AC[1]));
  ALU_1bit _3 (
    .AND(AND), .ADD(ADD), .DR(DR_2), .c_i(alu_1bit_2_c_i_1), .INPR(INPR_2), .INPR_in(INPR[2]), .COM(COM),
    .SHR(SHR), .AC_i_1(AC[3]), .SHL(SHL), .AC_i_1_2(AC[1]), .c_i_1(_3_c_i_1), .OUT(ALUOutput[2]),
    .DR_i(DR[2]), .AC_i(AC[2]));
  ALU_1bit alu_1bit_3 (
    .AND(AND), .ADD(ADD), .DR(DR_2), .c_i(_3_c_i_1), .INPR(INPR_2), .INPR_in(INPR[3]), .COM(COM), .SHR(SHR),
    .AC_i_1(AC[4]), .SHL(SHL), .AC_i_1_2(AC[2]), .c_i_1(alu_1bit_3_c_i_1), .OUT(ALUOutput[3]), .DR_i(DR[3]),
    .AC_i(AC[3]));
  ALU_1bit alu_1bit_4 (
    .AND(AND), .ADD(ADD), .DR(DR_2), .c_i(alu_1bit_3_c_i_1), .INPR(INPR_2), .INPR_in(INPR[4]), .COM(COM),
    .SHR(SHR), .AC_i_1(AC[5]), .SHL(SHL), .AC_i_1_2(AC[3]), .c_i_1(alu_1bit_4_c_i_1), .OUT(ALUOutput[4]),
    .DR_i(DR[4]), .AC_i(AC[4]));
  ALU_1bit alu_1bit_5 (
    .AND(AND), .ADD(ADD), .DR(DR_2), .c_i(alu_1bit_4_c_i_1), .INPR(INPR_2), .INPR_in(INPR[5]), .COM(COM),
    .SHR(SHR), .AC_i_1(AC[6]), .SHL(SHL), .AC_i_1_2(AC[4]), .c_i_1(alu_1bit_5_c_i_1), .OUT(ALUOutput[5]),
    .DR_i(DR[5]), .AC_i(AC[5]));
  ALU_1bit alu_1bit_6 (
    .AND(AND), .ADD(ADD), .DR(DR_2), .c_i(alu_1bit_5_c_i_1), .INPR(INPR_2), .INPR_in(INPR[6]), .COM(COM),
    .SHR(SHR), .AC_i_1(AC[7]), .SHL(SHL), .AC_i_1_2(AC[5]), .c_i_1(alu_1bit_6_c_i_1), .OUT(ALUOutput[6]),
    .DR_i(DR[6]), .AC_i(AC[6]));
  ALU_1bit alu_1bit_7 (
    .AND(AND), .ADD(ADD), .DR(DR_2), .c_i(alu_1bit_6_c_i_1), .INPR(INPR_2), .INPR_in(INPR[7]), .COM(COM),
    .SHR(SHR), .AC_i_1(AC[8]), .SHL(SHL), .AC_i_1_2(AC[6]), .c_i_1(alu_1bit_7_c_i_1), .OUT(ALUOutput[7]),
    .DR_i(DR[7]), .AC_i(AC[7]));
  ALU_1bit alu_1bit_8 (
    .AND(AND), .ADD(ADD), .DR(DR_2), .c_i(alu_1bit_7_c_i_1), .INPR(INPR_2), .INPR_in(1'b0), .COM(COM),
    .SHR(SHR), .AC_i_1(AC[9]), .SHL(SHL), .AC_i_1_2(AC[7]), .c_i_1(alu_1bit_8_c_i_1), .OUT(ALUOutput[8]),
    .DR_i(DR[8]), .AC_i(AC[8]));
  ALU_1bit alu_1bit_9 (
    .AND(AND), .ADD(ADD), .DR(DR_2), .c_i(alu_1bit_8_c_i_1), .INPR(INPR_2), .INPR_in(1'b0), .COM(COM),
    .SHR(SHR), .AC_i_1(AC[10]), .SHL(SHL), .AC_i_1_2(AC[8]), .c_i_1(alu_1bit_9_c_i_1), .OUT(ALUOutput[9]),
    .DR_i(DR[9]), .AC_i(AC[9]));
  ALU_1bit alu_1bit_10 (
    .AND(AND), .ADD(ADD), .DR(DR_2), .c_i(alu_1bit_9_c_i_1), .INPR(INPR_2), .INPR_in(1'b0), .COM(COM),
    .SHR(SHR), .AC_i_1(AC[11]), .SHL(SHL), .AC_i_1_2(AC[9]), .c_i_1(alu_1bit_10_c_i_1), .OUT(ALUOutput[10]),
    .DR_i(DR[10]), .AC_i(AC[10]));
  ALU_1bit alu_1bit_11 (
    .AND(AND), .ADD(ADD), .DR(DR_2), .c_i(alu_1bit_10_c_i_1), .INPR(INPR_2), .INPR_in(1'b0), .COM(COM),
    .SHR(SHR), .AC_i_1(AC[12]), .SHL(SHL), .AC_i_1_2(AC[10]), .c_i_1(alu_1bit_11_c_i_1), .OUT(ALUOutput[11]),
    .DR_i(DR[11]), .AC_i(AC[11]));
  ALU_1bit alu_1bit_12 (
    .AND(AND), .ADD(ADD), .DR(DR_2), .c_i(alu_1bit_11_c_i_1), .INPR(INPR_2), .INPR_in(1'b0), .COM(COM),
    .SHR(SHR), .AC_i_1(AC[13]), .SHL(SHL), .AC_i_1_2(AC[11]), .c_i_1(alu_1bit_12_c_i_1), .OUT(ALUOutput[12]),
    .DR_i(DR[12]), .AC_i(AC[12]));
  ALU_1bit alu_1bit_13 (
    .AND(AND), .ADD(ADD), .DR(DR_2), .c_i(alu_1bit_12_c_i_1), .INPR(INPR_2), .INPR_in(1'b0), .COM(COM),
    .SHR(SHR), .AC_i_1(AC[14]), .SHL(SHL), .AC_i_1_2(AC[12]), .c_i_1(alu_1bit_13_c_i_1), .OUT(ALUOutput[13]),
    .DR_i(DR[13]), .AC_i(AC[13]));
  ALU_1bit alu_1bit_14 (
    .AND(AND), .ADD(ADD), .DR(DR_2), .c_i(alu_1bit_13_c_i_1), .INPR(INPR_2), .INPR_in(1'b0), .COM(COM),
    .SHR(SHR), .AC_i_1(AC[15]), .SHL(SHL), .AC_i_1_2(AC[13]), .c_i_1(alu_1bit_14_c_i_1), .OUT(ALUOutput[14]),
    .DR_i(DR[14]), .AC_i(AC[14]));
  ALU_1bit alu_1bit_15 (
    .AND(AND), .ADD(ADD), .DR(DR_2), .c_i(alu_1bit_14_c_i_1), .INPR(INPR_2), .INPR_in(1'b0), .COM(COM),
    .SHR(SHR), .AC_i_1(E), .SHL(SHL), .AC_i_1_2(AC[14]), .c_i_1(alu_1bit_15_c_i_1), .OUT(ALUOutput[15]),
    .DR_i(DR[15]), .AC_i(AC[15]));
  and and_3 (and_3_out, alu_1bit_15_c_i_1, ADD);
  or or_3 (E_2, and_3_out, and_4_out, Shift);
  not not_1 (not_1_out, isShift);
  and and_4 (and_4_out, not_1_out, E);

  // Other names for the same wires on the sheet: Controler[6:0] = {SHL, SHR, COM, INPR_2, DR_2, ADD, AND}

  // Notes on the sheet:
  //   1
  //   2
  //   3
  //   4
  //   5
  //   6
  //   7
  //   8
  //   9
  //   10
  //   11
  //   12
  //   13
  //   14
  //   15
endmodule

module AC (
  input  [15:0] \input ,
  input  Load,
  input  INC,
  input  Clear,
  input  CLK,
  output [15:0] Output
);

  Counter #(.width(16), .max('hffff)) counter_1 (
    .load(Load), .D(\input ), .count(INC), .Q(Output), .clk(CLK), .clr(Clear));  // open: carry
endmodule

module AR (
  input  [15:0] \input ,
  input  Load,
  input  INC,
  input  Clear,
  input  CLK,
  output [15:0] Output
);

  Counter #(.width(12), .max('hfff)) counter_1 (
    .load(Load), .D(\input [11:0]), .count(INC), .Q(Output[11:0]), .clk(CLK), .clr(Clear));  // open: carry

  assign Output[15:12] = 4'b0000;
endmodule

module PC (
  input  [15:0] \input ,
  input  Load,
  input  INC,
  input  Clear,
  input  CLK,
  output [15:0] Output
);

  Counter #(.width(12), .max('hfff)) counter_1 (
    .load(Load), .D(\input [11:0]), .count(INC), .Q(Output[11:0]), .clk(CLK), .clr(Clear));  // open: carry

  assign Output[15:12] = 4'b0000;
endmodule

module DR (
  input  [15:0] \input ,
  input  Load,
  input  INC,
  input  Clear,
  input  CLK,
  output [15:0] Output
);

  Counter #(.width(16), .max('hffff)) counter_1 (
    .load(Load), .D(\input ), .count(INC), .Q(Output), .clk(CLK), .clr(Clear));  // open: carry
endmodule

module IR (
  input  [15:0] \input ,
  input  Load,
  input  CLK,
  output [15:0] Output
);

  Counter #(.width(16), .max('hffff)) counter_1 (
    .load(Load), .D(\input ), .count(1'b0), .Q(Output), .clk(CLK));  // open: carry, clr
endmodule

module TR (
  input  [15:0] \input ,
  input  Load,
  input  INC,
  input  Clear,
  input  CLK,
  output [15:0] Output
);

  Counter #(.width(16), .max('hffff)) counter_1 (
    .load(Load), .D(\input ), .count(INC), .Q(Output), .clk(CLK), .clr(Clear));  // open: carry
endmodule

module INPR (
  output [7:0] out_1
);

  Register register_1 (.Q(out_1));  // open: D, en, clk, clr
endmodule

module OUTR (
  input  [15:0] \input ,
  input  CLK,
  input  Load,
  output [7:0] out_4
);

  Counter counter_1 (.load(Load), .D(\input [7:0]), .count(1'b0), .Q(out_4), .clk(CLK));  // open: carry, clr
endmodule

module AC_ALU_Controler (
  input  [15:0] in_1,
  input  in_2,
  input  in_3,
  input  [3:0] SeqCntrInp,
  output AND,
  output ADD,
  output DR,
  output INPR,
  output COM,
  output SHR,
  output SHL,
  output INCREMENT_AC,
  output CLEAR_AC
);

  wire D0, D1, D2, D3, D4, D5, D6, D7, decoder_1_out8, decoder_1_out9, not_1_out, p, r_t, T0, T1, T2, T3, T4,
       T5, T6, T7, T10, T11, T12, T13, T14, T15;

  Decoder #(.select(4), .enable("false")) decoder_1 (
    .out0(T0), .out1(T1), .out2(T2), .out3(T3), .out4(T4), .out5(T5), .out6(T6), .out7(T7),
    .out8(decoder_1_out8), .out9(decoder_1_out9), .out10(T10), .out11(T11), .out12(T12), .out13(T13),
    .out14(T14), .out15(T15), .sel(SeqCntrInp));
  and and_1 (AND, D0, T5);
  and and_2 (ADD, T5, D1);
  and and_3 (DR, D2, T5);
  and and_4 (INPR, p, in_1[11]);
  and and_5 (COM, r_t, in_1[9]);
  and and_6 (SHR, r_t, in_1[7]);
  and and_7 (SHL, r_t, in_1[6]);
  and and_8 (INCREMENT_AC, r_t, in_1[5]);
  and and_9 (CLEAR_AC, r_t, in_1[11]);
  Decoder #(.select(3), .enable("false")) decoder_2 (
    .out0(D0), .out1(D1), .out2(D2), .out3(D3), .out4(D4), .out5(D5), .out6(D6), .out7(D7), .sel(in_1[14:12]));
  and and_10 (p, D7, in_3, T3);
  not not_1 (not_1_out, in_3);
  and and_11 (r_t, D7, not_1_out, T3);

  // Other names for the same wires on the sheet: I = in_3; B0 = in_1[0]; B1 = in_1[1]; B2 = in_1[2]; B3 = in_1[3];
  //   B4 = in_1[4]; B5 = in_1[5]; B6 = in_1[6]; B7 = in_1[7]; B8 = in_1[8]; B9 = in_1[9]; B10 = in_1[10];
  //   B11 = in_1[11]; R = in_2
endmodule

module AR_Controler (
  input  [15:0] in_1,
  input  in_2,
  input  in_3,
  input  [3:0] SeqCntrInp,
  output Load,
  output INR,
  output CLR
);

  wire and_1_out, and_2_out, and_3_out, D0, D1, D2, D3, D4, D5, D6, D7, decoder_1_out8, decoder_1_out9,
       not_1_out, not_2_out, not_3_out, p, r_t, T0, T1, T2, T3, T4, T5, T6, T7, T10, T11, T12, T13, T14, T15;

  Decoder #(.select(4), .enable("false")) decoder_1 (
    .out0(T0), .out1(T1), .out2(T2), .out3(T3), .out4(T4), .out5(T5), .out6(T6), .out7(T7),
    .out8(decoder_1_out8), .out9(decoder_1_out9), .out10(T10), .out11(T11), .out12(T12), .out13(T13),
    .out14(T14), .out15(T15), .sel(SeqCntrInp));
  not not_1 (not_1_out, D7);
  not not_2 (not_2_out, in_2);
  and and_1 (and_1_out, not_1_out, in_3, T3);
  and and_2 (and_2_out, T2, not_2_out);
  and and_3 (and_3_out, not_2_out, T0);
  and and_4 (INR, D5, T4);
  and and_5 (CLR, T0, in_2);
  or or_1 (Load, and_1_out, and_2_out, and_3_out);
  Decoder #(.select(3), .enable("false")) decoder_2 (
    .out0(D0), .out1(D1), .out2(D2), .out3(D3), .out4(D4), .out5(D5), .out6(D6), .out7(D7), .sel(in_1[14:12]));
  and and_6 (p, D7, in_3, T3);
  not not_3 (not_3_out, in_3);
  and and_7 (r_t, D7, not_3_out, T3);

  // Other names for the same wires on the sheet: I = in_3; B0 = in_1[0]; B1 = in_1[1]; B2 = in_1[2]; B3 = in_1[3];
  //   B4 = in_1[4]; B5 = in_1[5]; B6 = in_1[6]; B7 = in_1[7]; B8 = in_1[8]; B9 = in_1[9]; B10 = in_1[10];
  //   B11 = in_1[11]; R = in_2
endmodule

module PC_Controler (
  input  [15:0] IR,
  input  [15:0] AC,
  input  [15:0] DR,
  input  FGI,
  input  FGO,
  input  E,
  input  in_7,
  input  in_8,
  input  [3:0] SeqCntrInp,
  output Load,
  output INR,
  output CLR
);

  wire AC_t, and_1_out, and_2_out, and_4_out, and_5_out, and_6_out, and_7_out, and_8_out, and_9_out,
       and_10_out, and_11_out, and_12_out, D0, D1, D2, D3, D4, D5, D6, D7, decoder_1_out8, decoder_1_out9,
       DR_t, not_1_out, not_2_out, not_3_out, not_4_out, not_5_out, not_6_out, p, r_t, T0, T1, T2, T3, T4,
       T5, T6, T7, T10, T11, T12, T13, T14, T15;

  Decoder #(.select(4), .enable("false")) decoder_1 (
    .out0(T0), .out1(T1), .out2(T2), .out3(T3), .out4(T4), .out5(T5), .out6(T6), .out7(T7),
    .out8(decoder_1_out8), .out9(decoder_1_out9), .out10(T10), .out11(T11), .out12(T12), .out13(T13),
    .out14(T14), .out15(T15), .sel(SeqCntrInp));
  and and_1 (and_1_out, D4, T4);
  and and_2 (and_2_out, D5, T5);
  and and_3 (CLR, in_7, T1);
  or or_1 (Load, and_1_out, and_2_out);
  not not_1 (not_1_out, in_7);
  and and_4 (and_4_out, not_1_out, T1);
  and and_5 (and_5_out, in_7, T2);
  and and_6 (and_6_out, D6, T6, not_2_out);
  not not_2 (not_2_out, DR_t);
  and and_7 (and_7_out, r_t, IR[4], not_3_out);
  not not_3 (not_3_out, AC[15]);
  and and_8 (and_8_out, r_t, IR[3], AC[15]);
  and and_9 (and_9_out, r_t, IR[2], not_4_out);
  not not_4 (not_4_out, AC_t);
  and and_10 (and_10_out, r_t, IR[1], not_5_out);
  not not_5 (not_5_out, E);
  and and_11 (and_11_out, p, IR[9], FGI);
  and and_12 (and_12_out, p, FGO);
  Decoder #(.select(3), .enable("false")) decoder_2 (
    .out0(D0), .out1(D1), .out2(D2), .out3(D3), .out4(D4), .out5(D5), .out6(D6), .out7(D7), .sel(IR[14:12]));
  or or_2 (INR, and_4_out, and_5_out, and_6_out, and_7_out, and_8_out, and_9_out, and_10_out, and_11_out, and_12_out);
  or or_3 (AC_t, AC[0], AC[1], AC[2], AC[3], AC[4], AC[5], AC[6], AC[7], AC[8], AC[9], AC[10], AC[11], AC[12], AC[13], AC[14], AC[15], AC[15]);
  and and_13 (p, D7, in_8, T3);
  or or_4 (DR_t, DR[0], DR[1], DR[2], DR[3], DR[4], DR[5], DR[6], DR[7], DR[8], DR[9], DR[10], DR[11], DR[12], DR[13], DR[14], DR[15]);
  not not_6 (not_6_out, in_8);
  and and_14 (r_t, D7, not_6_out, T3);

  // Other names for the same wires on the sheet: AC_15 = AC[15]; I = in_8; B0 = IR[0]; B1 = IR[1]; B2 = IR[2];
  //   B3 = IR[3]; B4 = IR[4]; B5 = IR[5]; B6 = IR[6]; B7 = IR[7]; B8 = IR[8]; B9 = IR[9]; B10 = IR[10]; B11 = IR[11];
  //   R = in_7
endmodule

module DR_Controler (
  input  [15:0] in_1,
  input  in_2,
  input  in_3,
  input  [3:0] SeqCntrInp,
  output Load,
  output INR
);

  wire D0, D1, D2, D3, D4, D5, D6, D7, decoder_1_out8, decoder_1_out9, not_1_out, or_1_out, p, r_t, T0, T1,
       T2, T3, T4, T5, T6, T7, T10, T11, T12, T13, T14, T15;

  Decoder #(.select(4), .enable("false")) decoder_1 (
    .out0(T0), .out1(T1), .out2(T2), .out3(T3), .out4(T4), .out5(T5), .out6(T6), .out7(T7),
    .out8(decoder_1_out8), .out9(decoder_1_out9), .out10(T10), .out11(T11), .out12(T12), .out13(T13),
    .out14(T14), .out15(T15), .sel(SeqCntrInp));
  or or_1 (or_1_out, D0, D1, D2, D6);
  and and_1 (Load, or_1_out, T4);
  and and_2 (INR, D6, T5);
  Decoder #(.select(3), .enable("false")) decoder_2 (
    .out0(D0), .out1(D1), .out2(D2), .out3(D3), .out4(D4), .out5(D5), .out6(D6), .out7(D7), .sel(in_1[14:12]));
  and and_3 (p, D7, in_3, T3);
  not not_1 (not_1_out, in_3);
  and and_4 (r_t, D7, not_1_out, T3);

  // Other names for the same wires on the sheet: I = in_3; B0 = in_1[0]; B1 = in_1[1]; B2 = in_1[2]; B3 = in_1[3];
  //   B4 = in_1[4]; B5 = in_1[5]; B6 = in_1[6]; B7 = in_1[7]; B8 = in_1[8]; B9 = in_1[9]; B10 = in_1[10];
  //   B11 = in_1[11]; R = in_2
endmodule

module IR_Controler (
  input  [15:0] in_1,
  input  in_2,
  input  in_3,
  input  [3:0] SeqCntrInp,
  output Load
);

  wire D0, D1, D2, D3, D4, D5, D6, D7, decoder_1_out8, decoder_1_out9, not_1_out, not_2_out, p, r_t, T0, T1,
       T2, T3, T4, T5, T6, T7, T10, T11, T12, T13, T14, T15;

  Decoder #(.select(4), .enable("false")) decoder_1 (
    .out0(T0), .out1(T1), .out2(T2), .out3(T3), .out4(T4), .out5(T5), .out6(T6), .out7(T7),
    .out8(decoder_1_out8), .out9(decoder_1_out9), .out10(T10), .out11(T11), .out12(T12), .out13(T13),
    .out14(T14), .out15(T15), .sel(SeqCntrInp));
  not not_1 (not_1_out, in_2);
  and and_1 (Load, not_1_out, T1);
  Decoder #(.select(3), .enable("false")) decoder_2 (
    .out0(D0), .out1(D1), .out2(D2), .out3(D3), .out4(D4), .out5(D5), .out6(D6), .out7(D7), .sel(in_1[14:12]));
  and and_2 (p, D7, in_3, T3);
  not not_2 (not_2_out, in_3);
  and and_3 (r_t, D7, not_2_out, T3);

  // Other names for the same wires on the sheet: I = in_3; B0 = in_1[0]; B1 = in_1[1]; B2 = in_1[2]; B3 = in_1[3];
  //   B4 = in_1[4]; B5 = in_1[5]; B6 = in_1[6]; B7 = in_1[7]; B8 = in_1[8]; B9 = in_1[9]; B10 = in_1[10];
  //   B11 = in_1[11]; R = in_2
endmodule

module TR_Controler (
  input  [15:0] in_1,
  input  in_2,
  input  in_3,
  input  [3:0] SeqCntrInp,
  output Load
);

  wire D0, D1, D2, D3, D4, D5, D6, D7, decoder_1_out8, decoder_1_out9, not_1_out, p, r_t, T0, T1, T2, T3, T4,
       T5, T6, T7, T10, T11, T12, T13, T14, T15;

  Decoder #(.select(4), .enable("false")) decoder_1 (
    .out0(T0), .out1(T1), .out2(T2), .out3(T3), .out4(T4), .out5(T5), .out6(T6), .out7(T7),
    .out8(decoder_1_out8), .out9(decoder_1_out9), .out10(T10), .out11(T11), .out12(T12), .out13(T13),
    .out14(T14), .out15(T15), .sel(SeqCntrInp));
  and and_1 (Load, in_2, T0);
  Decoder #(.select(3), .enable("false")) decoder_2 (
    .out0(D0), .out1(D1), .out2(D2), .out3(D3), .out4(D4), .out5(D5), .out6(D6), .out7(D7), .sel(in_1[14:12]));
  and and_2 (p, D7, in_3, T3);
  not not_1 (not_1_out, in_3);
  and and_3 (r_t, D7, not_1_out, T3);

  // Other names for the same wires on the sheet: I = in_3; B0 = in_1[0]; B1 = in_1[1]; B2 = in_1[2]; B3 = in_1[3];
  //   B4 = in_1[4]; B5 = in_1[5]; B6 = in_1[6]; B7 = in_1[7]; B8 = in_1[8]; B9 = in_1[9]; B10 = in_1[10];
  //   B11 = in_1[11]; R = in_2
endmodule

module OUTR_Controler (
  input  [15:0] in_1,
  input  in_2,
  input  in_3,
  input  [3:0] SeqCntrInp,
  output Load
);

  wire D0, D1, D2, D3, D4, D5, D6, D7, decoder_1_out8, decoder_1_out9, not_1_out, p, r_t, T0, T1, T2, T3, T4,
       T5, T6, T7, T10, T11, T12, T13, T14, T15;

  Decoder #(.select(4), .enable("false")) decoder_1 (
    .out0(T0), .out1(T1), .out2(T2), .out3(T3), .out4(T4), .out5(T5), .out6(T6), .out7(T7),
    .out8(decoder_1_out8), .out9(decoder_1_out9), .out10(T10), .out11(T11), .out12(T12), .out13(T13),
    .out14(T14), .out15(T15), .sel(SeqCntrInp));
  and and_1 (Load, p, in_1[10]);
  Decoder #(.select(3), .enable("false")) decoder_2 (
    .out0(D0), .out1(D1), .out2(D2), .out3(D3), .out4(D4), .out5(D5), .out6(D6), .out7(D7), .sel(in_1[14:12]));
  and and_2 (p, D7, in_3, T3);
  not not_1 (not_1_out, in_3);
  and and_3 (r_t, D7, not_1_out, T3);

  // Other names for the same wires on the sheet: I = in_3; B0 = in_1[0]; B1 = in_1[1]; B2 = in_1[2]; B3 = in_1[3];
  //   B4 = in_1[4]; B5 = in_1[5]; B6 = in_1[6]; B7 = in_1[7]; B8 = in_1[8]; B9 = in_1[9]; B10 = in_1[10];
  //   B11 = in_1[11]; R = in_2
endmodule

module Memory_Controler (
  input  [15:0] in_1,
  input  in_2,
  input  in_3,
  input  [3:0] SeqCntrInp,
  output Read,
  output Write
);

  wire and_1_out, and_2_out, and_3_out, and_4_out, and_5_out, and_6_out, and_7_out, D0, D1, D2, D3, D4, D5,
       D6, D7, decoder_1_out8, decoder_1_out9, not_1_out, not_2_out, not_3_out, or_2_out, p, r_t, T0, T1, T2,
       T3, T4, T5, T6, T7, T10, T11, T12, T13, T14, T15;

  and and_1 (and_1_out, in_2, T1);
  and and_2 (and_2_out, D3, T4);
  and and_3 (and_3_out, D5, T4);
  and and_4 (and_4_out, D6, T6);
  Decoder #(.select(4), .enable("false")) decoder_1 (
    .out0(T0), .out1(T1), .out2(T2), .out3(T3), .out4(T4), .out5(T5), .out6(T6), .out7(T7),
    .out8(decoder_1_out8), .out9(decoder_1_out9), .out10(T10), .out11(T11), .out12(T12), .out13(T13),
    .out14(T14), .out15(T15), .sel(SeqCntrInp));
  or or_1 (Write, and_1_out, and_2_out, and_3_out, and_4_out);
  not not_1 (not_1_out, in_2);
  and and_5 (and_5_out, not_1_out, T1);
  not not_2 (not_2_out, D7);
  and and_6 (and_6_out, not_2_out, in_3, T3);
  or or_2 (or_2_out, D0, D1, D2, D6);
  and and_7 (and_7_out, or_2_out, T4);
  Decoder #(.select(3), .enable("false")) decoder_2 (
    .out0(D0), .out1(D1), .out2(D2), .out3(D3), .out4(D4), .out5(D5), .out6(D6), .out7(D7), .sel(in_1[14:12]));
  or or_3 (Read, and_5_out, and_6_out, and_7_out);
  and and_8 (p, D7, in_3, T3);
  not not_3 (not_3_out, in_3);
  and and_9 (r_t, D7, not_3_out, T3);

  // Other names for the same wires on the sheet: I = in_3; B0 = in_1[0]; B1 = in_1[1]; B2 = in_1[2]; B3 = in_1[3];
  //   B4 = in_1[4]; B5 = in_1[5]; B6 = in_1[6]; B7 = in_1[7]; B8 = in_1[8]; B9 = in_1[9]; B10 = in_1[10];
  //   B11 = in_1[11]; R = in_2
endmodule

module SC_Clear_Controler (
  input  [15:0] in_1,
  input  in_2,
  input  in_3,
  input  [3:0] SeqCntrInp,
  output Clear
);

  wire and_1_out, and_2_out, and_3_out, and_4_out, D0, D1, D2, D3, D4, D5, D6, D7, decoder_1_out8,
       decoder_1_out9, not_1_out, or_1_out, or_2_out, p, r_t, T0, T1, T2, T3, T4, T5, T6, T7, T10, T11, T12,
       T13, T14, T15;

  Decoder #(.select(4), .enable("false")) decoder_1 (
    .out0(T0), .out1(T1), .out2(T2), .out3(T3), .out4(T4), .out5(T5), .out6(T6), .out7(T7),
    .out8(decoder_1_out8), .out9(decoder_1_out9), .out10(T10), .out11(T11), .out12(T12), .out13(T13),
    .out14(T14), .out15(T15), .sel(SeqCntrInp));
  and and_1 (and_1_out, in_2, T2);
  or or_1 (or_1_out, D4, D3);
  or or_2 (or_2_out, D0, D1, D2, D5);
  and and_2 (and_2_out, D6, T6);
  and and_3 (and_3_out, or_1_out, T4);
  and and_4 (and_4_out, or_2_out, T5);
  or or_3 (Clear, and_1_out, and_3_out, and_4_out, and_2_out, r_t, p);
  Decoder #(.select(3), .enable("false")) decoder_2 (
    .out0(D0), .out1(D1), .out2(D2), .out3(D3), .out4(D4), .out5(D5), .out6(D6), .out7(D7), .sel(in_1[14:12]));
  and and_5 (p, D7, in_3, T3);
  not not_1 (not_1_out, in_3);
  and and_6 (r_t, D7, not_1_out, T3);

  // Other names for the same wires on the sheet: I = in_3; B0 = in_1[0]; B1 = in_1[1]; B2 = in_1[2]; B3 = in_1[3];
  //   B4 = in_1[4]; B5 = in_1[5]; B6 = in_1[6]; B7 = in_1[7]; B8 = in_1[8]; B9 = in_1[9]; B10 = in_1[10];
  //   B11 = in_1[11]; R = in_2
endmodule

module R_Controler (
  input  [15:0] in_1,
  input  IEN,
  input  FGI,
  input  FGO,
  input  in_5,
  input  [3:0] SeqCntrInp,
  output J,
  output K
);

  wire D0, D1, D2, D3, D4, D5, D6, D7, decoder_1_out8, decoder_1_out9, not_1_out, not_2_out, not_3_out,
       or_1_out, T0, T1, T2, T3, T4, T5, T6, T7, T10, T11, T12, T13, T14, T15;

  Decoder #(.select(4), .enable("false")) decoder_1 (
    .out0(T0), .out1(T1), .out2(T2), .out3(T3), .out4(T4), .out5(T5), .out6(T6), .out7(T7),
    .out8(decoder_1_out8), .out9(decoder_1_out9), .out10(T10), .out11(T11), .out12(T12), .out13(T13),
    .out14(T14), .out15(T15), .sel(SeqCntrInp));
  not not_1 (not_1_out, T0);
  not not_2 (not_2_out, T1);
  not not_3 (not_3_out, T2);
  or or_1 (or_1_out, FGI, FGO);
  and SET (J, not_1_out, not_2_out, not_3_out, IEN, or_1_out);
  and RESET (K, T2, in_5);
  Decoder #(.select(3), .enable("false")) decoder_2 (
    .out0(D0), .out1(D1), .out2(D2), .out3(D3), .out4(D4), .out5(D5), .out6(D6), .out7(D7), .sel(in_1[14:12]));

  // Other names for the same wires on the sheet: B0 = in_1[0]; B1 = in_1[1]; B2 = in_1[2]; B3 = in_1[3]; B4 = in_1[4];
  //   B5 = in_1[5]; B6 = in_1[6]; B7 = in_1[7]; B8 = in_1[8]; B9 = in_1[9]; B10 = in_1[10]; B11 = in_1[11]; R = in_5
endmodule

module I_Controler (
  input  [15:0] in_1,
  input  in_2,
  input  in_3,
  input  [3:0] SeqCntrInp,
  output J,
  output K
);

  wire and_1_out, D0, D1, D2, D3, D4, D5, D6, D7, decoder_1_out8, decoder_1_out9, not_1_out, not_2_out, T0,
       T1, T2, T3, T4, T5, T6, T7, T10, T11, T12, T13, T14, T15;

  Decoder #(.select(4), .enable("false")) decoder_1 (
    .out0(T0), .out1(T1), .out2(T2), .out3(T3), .out4(T4), .out5(T5), .out6(T6), .out7(T7),
    .out8(decoder_1_out8), .out9(decoder_1_out9), .out10(T10), .out11(T11), .out12(T12), .out13(T13),
    .out14(T14), .out15(T15), .sel(SeqCntrInp));
  not not_1 (not_1_out, in_1[15]);
  not not_2 (not_2_out, in_2);
  and and_1 (and_1_out, not_2_out, T2);
  and and_2 (J, in_1[15], and_1_out);
  and and_3 (K, not_1_out, and_1_out);
  Decoder #(.select(3), .enable("false")) decoder_2 (
    .out0(D0), .out1(D1), .out2(D2), .out3(D3), .out4(D4), .out5(D5), .out6(D6), .out7(D7), .sel(in_1[14:12]));

  // Other names for the same wires on the sheet: I = in_3; B0 = in_1[0]; B1 = in_1[1]; B2 = in_1[2]; B3 = in_1[3];
  //   B4 = in_1[4]; B5 = in_1[5]; B6 = in_1[6]; B7 = in_1[7]; B8 = in_1[8]; B9 = in_1[9]; B10 = in_1[10];
  //   B11 = in_1[11]; R = in_2
endmodule

module S_Controler (
  input  [15:0] in_1,
  input  in_2,
  input  in_3,
  input  [3:0] SeqCntrInp,
  output J,
  output K
);

  wire D0, D1, D2, D3, D4, D5, D6, D7, decoder_1_out8, decoder_1_out9, not_1_out, p, r_t, T0, T1, T2, T3, T4,
       T5, T6, T7, T10, T11, T12, T13, T14, T15;

  Decoder #(.select(4), .enable("false")) decoder_1 (
    .out0(T0), .out1(T1), .out2(T2), .out3(T3), .out4(T4), .out5(T5), .out6(T6), .out7(T7),
    .out8(decoder_1_out8), .out9(decoder_1_out9), .out10(T10), .out11(T11), .out12(T12), .out13(T13),
    .out14(T14), .out15(T15), .sel(SeqCntrInp));
  and and_1 (J, r_t, in_1[0]);
  Decoder #(.select(3), .enable("false")) decoder_2 (
    .out0(D0), .out1(D1), .out2(D2), .out3(D3), .out4(D4), .out5(D5), .out6(D6), .out7(D7), .sel(in_1[14:12]));
  and and_2 (p, D7, in_3, T3);
  not not_1 (not_1_out, in_3);
  and and_3 (r_t, D7, not_1_out, T3);

  assign K = 1'b1;

  // Other names for the same wires on the sheet: I = in_3; B0 = in_1[0]; B1 = in_1[1]; B2 = in_1[2]; B3 = in_1[3];
  //   B4 = in_1[4]; B5 = in_1[5]; B6 = in_1[6]; B7 = in_1[7]; B8 = in_1[8]; B9 = in_1[9]; B10 = in_1[10];
  //   B11 = in_1[11]; R = in_2
endmodule

module E_Controler (
  input  [15:0] in_1,
  input  in_2,
  input  in_3,
  input  in_4,
  input  [3:0] SeqCntrInp,
  output J,
  output K
);

  wire and_1_out, and_2_out, and_3_out, and_4_out, D0, D1, D2, D3, D4, D5, D6, D7, decoder_1_out8,
       decoder_1_out9, not_1_out, not_2_out, not_3_out, or_1_out, p, r_t, T0, T1, T2, T3, T4, T5, T6, T7,
       T10, T11, T12, T13, T14, T15;

  not not_1 (not_1_out, in_2);
  not not_2 (not_2_out, or_1_out);
  or or_1 (or_1_out, and_2_out, and_1_out);
  and and_1 (and_1_out, r_t, in_1[8]);
  and and_2 (and_2_out, r_t, in_1[10]);
  Decoder #(.select(4), .enable("false")) decoder_1 (
    .out0(T0), .out1(T1), .out2(T2), .out3(T3), .out4(T4), .out5(T5), .out6(T6), .out7(T7),
    .out8(decoder_1_out8), .out9(decoder_1_out9), .out10(T10), .out11(T11), .out12(T12), .out13(T13),
    .out14(T14), .out15(T15), .sel(SeqCntrInp));
  and and_3 (and_3_out, in_2, not_2_out);
  and and_4 (and_4_out, not_1_out, not_2_out);
  or or_2 (J, and_3_out, and_1_out);
  or or_3 (K, and_4_out, and_1_out, and_2_out);
  Decoder #(.select(3), .enable("false")) decoder_2 (
    .out0(D0), .out1(D1), .out2(D2), .out3(D3), .out4(D4), .out5(D5), .out6(D6), .out7(D7), .sel(in_1[14:12]));
  and and_5 (p, D7, in_4, T3);
  not not_3 (not_3_out, in_4);
  and and_6 (r_t, D7, not_3_out, T3);

  // Other names for the same wires on the sheet: ALU_E_OUT = in_2; I = in_4; B0 = in_1[0]; B1 = in_1[1]; B2 = in_1[2];
  //   B3 = in_1[3]; B4 = in_1[4]; B5 = in_1[5]; B6 = in_1[6]; B7 = in_1[7]; B8 = in_1[8]; B9 = in_1[9];
  //   B10 = in_1[10]; B11 = in_1[11]; R = in_3
endmodule

module IEN_Controler (
  input  [15:0] in_1,
  input  in_2,
  input  in_3,
  input  [3:0] SeqCntrInp,
  output J,
  output K
);

  wire and_1_out, and_2_out, D0, D1, D2, D3, D4, D5, D6, D7, decoder_1_out8, decoder_1_out9, not_1_out, p,
       r_t, T0, T1, T2, T3, T4, T5, T6, T7, T10, T11, T12, T13, T14, T15;

  and and_1 (and_1_out, in_2, T2);
  and and_2 (and_2_out, p, in_1[6]);
  Decoder #(.select(4), .enable("false")) decoder_1 (
    .out0(T0), .out1(T1), .out2(T2), .out3(T3), .out4(T4), .out5(T5), .out6(T6), .out7(T7),
    .out8(decoder_1_out8), .out9(decoder_1_out9), .out10(T10), .out11(T11), .out12(T12), .out13(T13),
    .out14(T14), .out15(T15), .sel(SeqCntrInp));
  or or_1 (K, and_1_out, and_2_out);
  and and_3 (J, p, in_1[7]);
  Decoder #(.select(3), .enable("false")) decoder_2 (
    .out0(D0), .out1(D1), .out2(D2), .out3(D3), .out4(D4), .out5(D5), .out6(D6), .out7(D7), .sel(in_1[14:12]));
  and and_4 (p, D7, in_3, T3);
  not not_1 (not_1_out, in_3);
  and and_5 (r_t, D7, not_1_out, T3);

  // Other names for the same wires on the sheet: I = in_3; B0 = in_1[0]; B1 = in_1[1]; B2 = in_1[2]; B3 = in_1[3];
  //   B4 = in_1[4]; B5 = in_1[5]; B6 = in_1[6]; B7 = in_1[7]; B8 = in_1[8]; B9 = in_1[9]; B10 = in_1[10];
  //   B11 = in_1[11]; R = in_2
endmodule

module FGI_Controler (
  input  [15:0] in_1,
  input  in_2,
  input  in_3,
  input  [3:0] SeqCntrInp,
  output J,
  output K
);

  wire D0, D1, D2, D3, D4, D5, D6, D7, decoder_1_out8, decoder_1_out9, not_1_out, p, r_t, T0, T1, T2, T3, T4,
       T5, T6, T7, T10, T11, T12, T13, T14, T15;

  Decoder #(.select(4), .enable("false")) decoder_1 (
    .out0(T0), .out1(T1), .out2(T2), .out3(T3), .out4(T4), .out5(T5), .out6(T6), .out7(T7),
    .out8(decoder_1_out8), .out9(decoder_1_out9), .out10(T10), .out11(T11), .out12(T12), .out13(T13),
    .out14(T14), .out15(T15), .sel(SeqCntrInp));
  and and_1 (K, p, in_1[11]);
  Decoder #(.select(3), .enable("false")) decoder_2 (
    .out0(D0), .out1(D1), .out2(D2), .out3(D3), .out4(D4), .out5(D5), .out6(D6), .out7(D7), .sel(in_1[14:12]));
  and and_2 (p, D7, in_3, T3);
  not not_1 (not_1_out, in_3);
  and and_3 (r_t, D7, not_1_out, T3);

  assign J = 1'b0;

  // Other names for the same wires on the sheet: I = in_3; B0 = in_1[0]; B1 = in_1[1]; B2 = in_1[2]; B3 = in_1[3];
  //   B4 = in_1[4]; B5 = in_1[5]; B6 = in_1[6]; B7 = in_1[7]; B8 = in_1[8]; B9 = in_1[9]; B10 = in_1[10];
  //   B11 = in_1[11]; R = in_2
endmodule

module FGO_Controler (
  input  [15:0] in_1,
  input  in_2,
  input  in_3,
  input  [3:0] SeqCntrInp,
  output J,
  output K
);

  wire D0, D1, D2, D3, D4, D5, D6, D7, decoder_1_out8, decoder_1_out9, not_1_out, p, r_t, T0, T1, T2, T3, T4,
       T5, T6, T7, T10, T11, T12, T13, T14, T15;

  Decoder #(.select(4), .enable("false")) decoder_1 (
    .out0(T0), .out1(T1), .out2(T2), .out3(T3), .out4(T4), .out5(T5), .out6(T6), .out7(T7),
    .out8(decoder_1_out8), .out9(decoder_1_out9), .out10(T10), .out11(T11), .out12(T12), .out13(T13),
    .out14(T14), .out15(T15), .sel(SeqCntrInp));
  and and_1 (K, p, in_1[10]);
  Decoder #(.select(3), .enable("false")) decoder_2 (
    .out0(D0), .out1(D1), .out2(D2), .out3(D3), .out4(D4), .out5(D5), .out6(D6), .out7(D7), .sel(in_1[14:12]));
  and and_2 (p, D7, in_3, T3);
  not not_1 (not_1_out, in_3);
  and and_3 (r_t, D7, not_1_out, T3);

  assign J = 1'b0;

  // Other names for the same wires on the sheet: I = in_3; B0 = in_1[0]; B1 = in_1[1]; B2 = in_1[2]; B3 = in_1[3];
  //   B4 = in_1[4]; B5 = in_1[5]; B6 = in_1[6]; B7 = in_1[7]; B8 = in_1[8]; B9 = in_1[9]; B10 = in_1[10];
  //   B11 = in_1[11]; R = in_2
endmodule

module Bus_Controler (
  input  [15:0] in_1,
  input  in_2,
  input  in_3,
  input  [3:0] SeqCntrInp,
  output [2:0] out_5
);

  wire and_1_out, and_2_out, and_3_out, and_4_out, and_5_out, and_6_out, and_7_out, and_8_out, and_9_out,
       and_10_out, and_11_out, and_12_out, D0, D1, D2, D3, D4, D5, D6, D7, decoder_1_out8, decoder_1_out9,
       not_1_out, not_2_out, not_3_out, not_4_out, or_1_out, or_2_out, or_3_out, or_4_out, or_5_out,
       or_6_out, p, r_t, T0, T1, T2, T3, T4, T5, T6, T7, T10, T11, T12, T13, T14, T15;

  and and_1 (and_1_out, D4, T4);
  and and_2 (and_2_out, D5, T5);
  and and_3 (and_3_out, D5, T4);
  and and_4 (and_4_out, D2, T5);
  and and_5 (and_5_out, D6, T6);
  and and_6 (and_6_out, D3, T4);
  and and_7 (and_7_out, p, in_1[10]);
  not not_1 (not_1_out, in_2);
  and and_8 (and_8_out, not_1_out, T2);
  and and_9 (and_9_out, in_2, T1);
  not not_2 (not_2_out, in_2);
  and and_10 (and_10_out, not_2_out, T1);
  not not_3 (not_3_out, D7);
  and and_11 (and_11_out, not_3_out, in_3, T3);
  or or_1 (or_1_out, D0, D1, D2, D6);
  Decoder #(.select(4), .enable("false")) decoder_1 (
    .out0(T0), .out1(T1), .out2(T2), .out3(T3), .out4(T4), .out5(T5), .out6(T6), .out7(T7),
    .out8(decoder_1_out8), .out9(decoder_1_out9), .out10(T10), .out11(T11), .out12(T12), .out13(T13),
    .out14(T14), .out15(T15), .sel(SeqCntrInp));
  or or_2 (or_2_out, and_1_out, and_2_out);
  or or_3 (or_3_out, T0, and_3_out);
  or or_4 (or_4_out, and_4_out, and_5_out);
  or or_5 (or_5_out, and_6_out, and_7_out);
  and and_12 (and_12_out, T4, or_1_out);
  or or_6 (or_6_out, and_10_out, and_11_out, and_12_out);
  Decoder #(.select(3), .enable("false")) decoder_2 (
    .out0(D0), .out1(D1), .out2(D2), .out3(D3), .out4(D4), .out5(D5), .out6(D6), .out7(D7), .sel(in_1[14:12]));
  Priority_Encoder priority_encoder_1 (
    .in0(1'b0), .in1(or_2_out), .in2(or_3_out), .in3(or_4_out), .in4(or_5_out), .in5(and_8_out),
    .in6(and_9_out), .in7(or_6_out), .out(out_5));  // open: en_in, gs, en_out
  and and_13 (p, D7, in_3, T3);
  not not_4 (not_4_out, in_3);
  and and_14 (r_t, D7, not_4_out, T3);

  // Other names for the same wires on the sheet: I = in_3; B0 = in_1[0]; B1 = in_1[1]; B2 = in_1[2]; B3 = in_1[3];
  //   B4 = in_1[4]; B5 = in_1[5]; B6 = in_1[6]; B7 = in_1[7]; B8 = in_1[8]; B9 = in_1[9]; B10 = in_1[10];
  //   B11 = in_1[11]; R = in_2
endmodule

module temp (
  input  [6:0] inp_str,
  input  CLK,
  input  [20:0] inp_pat,
  input  [3:0] in_4,
  input  in_5,
  input  in_6,
  input  in_7,
  output out_8,
  output is_rec,
  output [4:0] out_10,
  output [4:0] out_11,
  output [4:0] out_12,
  output [4:0] out_13,
  output [4:0] out_14
);

  wire and_1_out, CLK_SLOW, clock_1_out, clock_2_out, comparator_1_eq, comparator_2_eq, comparator_3_eq,
       controlled_buffer_1_out, counter_1_carry, decoder_1_out4, down, keyboard_1_avail, ld, left, not_2_out,
       not_3_out, or_1_out, or_2_out, reset_out, right, shift_register_1_out, start_out, up;
  wire [1:0] joystick_1_x, joystick_1_y, S;
  wire [2:0] counter_2_q;
  wire [4:0] i1, i2, i3, i4, i5, sl1, sl2, sl3, sl4, sl5, sr1, sr2, sr3, sr4, sr5, undriven, undriven_2,
       undriven_3, undriven_4, undriven_5;
  wire [6:0] E1, E2, E3, keyboard_1_data, keyboard_2_data, keyboard_3_data, keyboard_4_data;

  Clock clock_1 (.out(clock_1_out));
  Counter #(.width(3), .max('h7)) counter_1 (
    .carry(counter_1_carry), .clk(clock_1_out));  // open: load, D, count, Q, clr
  assign controlled_buffer_1_out = keyboard_1_avail ? counter_1_carry : 1'bz;  // Controlled_Buffer controlled_buffer_1
  Keyboard keyboard_1 (
    .clk(controlled_buffer_1_out), .re(1'b1), .avail(keyboard_1_avail), .data(keyboard_1_data));  // open: clr
  Keyboard #(.buflen(1)) keyboard_2 (.data(keyboard_2_data));  // open: clk, re, clr, avail
  Keyboard #(.buflen(1)) keyboard_3 (.data(keyboard_3_data));  // open: clk, re, clr, avail
  Keyboard #(.buflen(1)) keyboard_4 (.data(keyboard_4_data));  // open: clk, re, clr, avail
  Joystick #(.bits(2)) joystick_1 (.x(joystick_1_x), .y(joystick_1_y));
  Button start (.out(start_out));
  Button reset (.out(reset_out));
  Clock clock_2 (.out(clock_2_out));
  DotMatrix #(.matrixrows(5)) dotmatrix_1 (
    .col0(undriven_3), .col1(undriven_4), .col2(undriven), .col3(undriven_5), .col4(undriven_2));
  Counter #(.width(3), .max('h7)) counter_2 (.Q(counter_2_q), .clk(CLK));  // open: load, D, count, carry, clr
  or or_1 (or_1_out, counter_2_q[0], counter_2_q[1], counter_2_q[2]);
  Multiplexer #(.select(2), .width(5)) multiplexer_1 (
    .in0(out_14), .in1(out_11), .in2(sr1), .in3(sl1), .out(i1), .sel(S));  // open: en
  Multiplexer #(.select(2), .width(5)) multiplexer_2 (
    .in0(out_10), .in1(out_12), .in2(sr2), .in3(sl2), .out(i2), .sel(S));  // open: en
  Multiplexer #(.select(2), .width(5)) multiplexer_3 (
    .in0(out_11), .in1(out_13), .in2(sr3), .in3(sl3), .out(i3), .sel(S));  // open: en
  Multiplexer #(.select(2), .width(5)) multiplexer_4 (
    .in0(out_12), .in1(out_14), .in2(sr4), .in3(sl4), .out(i4), .sel(S));  // open: en
  Multiplexer #(.select(2), .width(5)) multiplexer_5 (
    .in0(out_13), .in1(out_10), .in2(sr5), .in3(sl5), .out(i5), .sel(S));  // open: en
  not not_1 (CLK_SLOW, or_1_out);
  Shifter #(.width(5), .shift("rl")) shifter_1 (.in(out_10), .\dist (3'b001), .out(sl1));
  Shifter #(.width(5), .shift("rl")) shifter_2 (.in(out_11), .\dist (3'b001), .out(sl2));
  Shifter #(.width(5), .shift("rl")) shifter_3 (.in(out_12), .\dist (3'b001), .out(sl3));
  Shifter #(.width(5), .shift("rl")) shifter_4 (.in(out_13), .\dist (3'b001), .out(sl4));
  Shifter #(.width(5), .shift("rl")) shifter_5 (.in(out_14), .\dist (3'b001), .out(sl5));
  not not_2 (not_2_out, CLK_SLOW);
  Shift_Register #(.length(7)) shift_register_1 (
    .shift(not_2_out), .clk(CLK), .out(shift_register_1_out), .load(CLK_SLOW), .d0(inp_str[6]),
    .d1(inp_str[5]), .d2(inp_str[4]), .d3(inp_str[3]), .d4(inp_str[2]), .d5(inp_str[1]), .d6(inp_str[0]));  // open: in, clr, q0, q1, q2, q3, q4, q5, q6
  Shifter #(.width(5), .shift("rr")) shifter_6 (.in(out_10), .\dist (3'b001), .out(sr1));
  Shifter #(.width(5), .shift("rr")) shifter_7 (.in(out_11), .\dist (3'b001), .out(sr2));
  Shift_Register #(.length(5)) shift_register_2 (
    .shift(1'b0), .clk(CLK), .load(ld), .clr(in_7), .d0(i1[4]), .q0(out_10[4]), .d1(i1[3]), .q1(out_10[3]),
    .d2(i1[2]), .q2(out_10[2]), .d3(i1[1]), .q3(out_10[1]), .d4(i1[0]), .q4(out_10[0]));  // open: in, out
  Shifter #(.width(5), .shift("rr")) shifter_8 (.in(out_12), .\dist (3'b001), .out(sr3));
  Shifter #(.width(5), .shift("rr")) shifter_9 (.in(out_13), .\dist (3'b001), .out(sr4));
  Shift_Register #(.length(5)) shift_register_3 (
    .shift(1'b0), .clk(CLK), .load(ld), .clr(in_7), .d0(i2[4]), .q0(out_11[4]), .d1(i2[3]), .q1(out_11[3]),
    .d2(i2[2]), .q2(out_11[2]), .d3(i2[1]), .q3(out_11[1]), .d4(i2[0]), .q4(out_11[0]));  // open: in, out
  Shifter #(.width(5), .shift("rr")) shifter_10 (.in(out_14), .\dist (3'b001), .out(sr5));
  Shift_Register #(.length(5)) shift_register_4 (
    .shift(in_6), .in(1'b1), .clk(or_2_out), .load(ld), .clr(in_7), .d0(i3[4]), .q0(out_12[4]), .d1(i3[3]),
    .q1(out_12[3]), .d2(i3[2]), .q2(out_12[2]), .d3(i3[1]), .q3(out_12[1]), .d4(i3[0]), .q4(out_12[0]));  // open: out
  or or_2 (or_2_out, CLK, in_6);
  Shift_Register #(.length(5)) shift_register_5 (
    .shift(1'b0), .clk(CLK), .load(ld), .clr(in_7), .d0(i4[4]), .q0(out_13[4]), .d1(i4[3]), .q1(out_13[3]),
    .d2(i4[2]), .q2(out_13[2]), .d3(i4[1]), .q3(out_13[1]), .d4(i4[0]), .q4(out_13[0]));  // open: in, out
  Shift_Register #(.length(5)) shift_register_6 (
    .shift(1'b0), .clk(CLK), .load(ld), .clr(in_7), .d0(i5[4]), .q0(out_14[4]), .d1(i5[3]), .q1(out_14[3]),
    .d2(i5[2]), .q2(out_14[2]), .d3(i5[1]), .q3(out_14[1]), .d4(i5[0]), .q4(out_14[0]));  // open: in, out
  not not_3 (not_3_out, CLK_SLOW);
  Shift_Register #(.length(21)) shift_register_7 (
    .shift(not_3_out), .in(shift_register_1_out), .clk(CLK), .q0(E3[6]), .q1(E3[5]), .q2(E3[4]), .q3(E3[3]),
    .q4(E3[2]), .q5(E3[1]), .q6(E3[0]), .q7(E2[6]), .q8(E2[5]), .q9(E2[4]), .q10(E2[3]), .q11(E2[2]),
    .q12(E2[1]), .q13(E2[0]), .q14(E1[6]), .q15(E1[5]), .q16(E1[4]), .q17(E1[3]), .q18(E1[2]), .q19(E1[1]),
    .q20(E1[0]));  // open: out, load, clr, d0, d1, d2, d3, d4, d5, d6, d7, d8, d9, d10, d11, d12, d13, d14, d15, d16, d17, d18, d19, d20
  Comparator #(.width(7), .mode("unsigned")) comparator_1 (
    .a(inp_pat[6:0]), .b(E1), .eq(comparator_1_eq));  // open: gt, lt
  Comparator #(.width(7), .mode("unsigned")) comparator_2 (
    .a(inp_pat[13:7]), .b(E2), .eq(comparator_2_eq));  // open: gt, lt
  Comparator #(.width(7), .mode("unsigned")) comparator_3 (
    .a(inp_pat[20:14]), .b(E3), .eq(comparator_3_eq));  // open: gt, lt
  and and_1 (and_1_out, comparator_1_eq, comparator_2_eq, comparator_3_eq, CLK_SLOW);
  Decoder #(.select(4)) decoder_1 (
    .out4(decoder_1_out4), .out6(up), .out9(left), .out11(right), .out14(down), .sel(in_4));  // open: out0, out1, out2, out3, out5, out7, out8, out10, out12, out13, out15, en
  Priority_Encoder #(.select(2)) priority_encoder_1 (
    .in0(right), .in1(left), .in2(down), .in3(up), .out(S), .gs(ld));  // open: en_out, en_in
  S_R_Flip_Flop s_r_ff_1 (.S(and_1_out), .clk(CLK), .R(decoder_1_out4), .Q(is_rec));  // open: Qn, preset, reset, en

  assign in_5 = CLK;
  // also tied to GND on the sheet: decoder_1_out4

  // Other names for the same wires on the sheet: Inp1[6:0] = inp_pat[6:0]; Inp2[6:0] = inp_pat[13:7];
  //   Inp3[6:0] = inp_pat[20:14]; o1[4:0] = out_10; o2[4:0] = out_11; o3[4:0] = out_12; o4[4:0] = out_13;
  //   o5[4:0] = out_14; reset = in_7; start = in_6

  // Notes on the sheet:
  //   CLk
  //   inp_str
  //   pattern
endmodule
